# Fritzing sketch Conexion Motores (saved by Fritzing 0.9.3b)

parts:
  S1 = H-Bridge with L298N
  Componente2 = Arduino Uno (Rev3) - ICSP
  M1 = DC Motor
  M2 = DC Motor
  Power_plug1 = Power plug

nets:
  12V: S1.12V, Power_plug1.VCC
  GND: S1.GND, Power_plug1.GND
  5V: S1.5V, Componente2.5V
  N1: S1.ENA, Componente2.D6_PWM
  N2: S1.IN1, Componente2.D8
  N3: S1.IN2, Componente2.D7
  N4: S1.IN3, Componente2.D4
  N5: S1.IN4, Componente2.D3_PWM
  N6: S1.ENB, Componente2.D5_PWM
  N7: S1.M1-01, M2.pin_2
  N8: S1.M1-02, M2.pin_1
  N9: S1.M2-01, M1.pin_2
  N10: S1.M2-02, M1.pin_1

custom parts:
  H-Bridge with L298N: h-bridge
