# Fritzing sketch ultrasonico (saved by Fritzing 0.9.3b)

parts:
  hc-sr1 = hc-sr04
  Componente1 = Arduino Uno (Rev3) - ICSP

nets:
  VCC: hc-sr1.VCC, Componente1.5V
  N1: hc-sr1.Trig, Componente1.D13/SCK
  N2: hc-sr1.Echo, Componente1.D12/MISO
  GND: hc-sr1.GND, Componente1.GND
